// Logisim project processador_8_bits.circ as structural Verilog: 6 circuits, main circuit main
module main (
  input  Count_Enable,
  input  Counter_OE,
  input  OE_MBR,
  input  WE_MBR,
  input  Internal_OE,
  input  WE_RAM,
  input  OE_IR,
  input  OE_MAR,
  input  OE_RAM,
  input  WE_IR,
  input  WE_MAR,
  input  WE_A,
  input  OE_Output,
  input  WE_Output,
  input  OE,
  input  WE_B,
  output [3:0] Content_Of_Counter,
  output [7:0] MBR_Content,
  output [7:0] IR_Content,
  output [3:0] MAR_Content,
  output [7:0] Reg_A_Content,
  output [7:0] ALU_Result,
  output [7:0] out_23,
  output [7:0] Reg_B_Content
);

  wire [3:0] bitselector_1_out, undriven_2;
  wire [7:0] bit_extender_1_out, controlled_buffer_1_out, undriven;
  wire [31:0] decimal_decoder_1_dout, decimal_decoder_2_dout, decimal_decoder_3_dout, decimal_decoder_4_dout;

  assign controlled_buffer_1_out = Internal_OE ? MBR_Content : 8'bz;  // Controlled_Buffer controlled_buffer_1
  Registrador MBR (
    .OE(OE_MBR), .Clock(OE_MBR), .WE(WE_MBR), .Din(controlled_buffer_1_out), .Storade_Data(MBR_Content),
    .Dout(controlled_buffer_1_out));
  LED L7 (.in(controlled_buffer_1_out[7]));
  LED L6 (.in(controlled_buffer_1_out[6]));
  LED L5 (.in(controlled_buffer_1_out[5]));
  LED L4 (.in(controlled_buffer_1_out[4]));
  LED L3 (.in(controlled_buffer_1_out[3]));
  LED L2 (.in(controlled_buffer_1_out[2]));
  LED L1 (.in(controlled_buffer_1_out[1]));
  LED D0 (.in(controlled_buffer_1_out[0]));
  LED L0 (.in(controlled_buffer_1_out[0]));
  LED D3 (.in(controlled_buffer_1_out[3]));
  LED D4 (.in(controlled_buffer_1_out[4]));
  LED D1 (.in(controlled_buffer_1_out[1]));
  LED D2 (.in(controlled_buffer_1_out[2]));
  LED D5 (.in(controlled_buffer_1_out[5]));
  LED D6 (.in(controlled_buffer_1_out[6]));
  LED D7 (.in(controlled_buffer_1_out[7]));
  Clock Clock_1 (.out(OE_MBR));
  BitSelector #(.group(4)) bitselector_1 (.in(undriven), .out(bitselector_1_out), .sel(1'b0));
  Registrador Instruction_Register (
    .OE(OE_IR), .Clock(OE_MBR), .WE(WE_IR), .Din(controlled_buffer_1_out), .Storade_Data(IR_Content),
    .Dout(undriven));
  Registrador Register_A (
    .Clock(OE_MBR), .WE(WE_A), .Din(controlled_buffer_1_out), .Storade_Data(Reg_A_Content));  // open: OE, Dout
  Registrador Register_B (
    .Clock(OE_MBR), .WE(WE_B), .Din(controlled_buffer_1_out), .Storade_Data(Reg_B_Content));  // open: OE, Dout
  ALU ALU_1 (
    .Reg_A(Reg_A_Content), .Dout(controlled_buffer_1_out), .Reg_B(Reg_B_Content), .OE(OE),
    .ALU_Result(ALU_Result));  // open: Carry_Out
  Decimal_Decoder decimal_decoder_1 (
    .in_1(Reg_A_Content),
    .Dout({decimal_decoder_1_dout[31:28], decimal_decoder_1_dout[31:28], decimal_decoder_1_dout[23:0]}));
  _7_Segment_Display u_7_segment_display_1 (
    .g(decimal_decoder_2_dout[15]), .f(decimal_decoder_2_dout[14]), .a(decimal_decoder_2_dout[13]),
    .b(decimal_decoder_2_dout[12]), .e(decimal_decoder_2_dout[31]), .d(decimal_decoder_2_dout[30]),
    .c(decimal_decoder_2_dout[29]), .dp(decimal_decoder_2_dout[28]));
  Counter #(.max('h3), .width(4)) Program_Counter (
    .count(Count_Enable), .clk(OE_MBR), .D(bitselector_1_out), .Q(Content_Of_Counter));  // open: clr, load, up, carry
  _7_Segment_Display u_7_segment_display_2 (
    .g(decimal_decoder_1_dout[15]), .f(decimal_decoder_1_dout[14]), .a(decimal_decoder_1_dout[13]),
    .b(decimal_decoder_1_dout[12]), .e(decimal_decoder_1_dout[31]), .d(decimal_decoder_1_dout[30]),
    .c(decimal_decoder_1_dout[29]), .dp(decimal_decoder_1_dout[28]));
  _7_Segment_Display u_7_segment_display_3 (
    .g(decimal_decoder_1_dout[11]), .f(decimal_decoder_1_dout[10]), .a(decimal_decoder_1_dout[9]),
    .b(decimal_decoder_1_dout[8]), .e(decimal_decoder_1_dout[31]), .d(decimal_decoder_1_dout[30]),
    .c(decimal_decoder_1_dout[29]), .dp(decimal_decoder_1_dout[28]));
  _7_Segment_Display u_7_segment_display_4 (
    .g(decimal_decoder_2_dout[11]), .f(decimal_decoder_2_dout[10]), .a(decimal_decoder_2_dout[9]),
    .b(decimal_decoder_2_dout[8]), .e(decimal_decoder_2_dout[31]), .d(decimal_decoder_2_dout[30]),
    .c(decimal_decoder_2_dout[29]), .dp(decimal_decoder_2_dout[28]));
  _7_Segment_Display u_7_segment_display_5 (
    .g(decimal_decoder_2_dout[7]), .f(decimal_decoder_2_dout[6]), .a(decimal_decoder_2_dout[5]),
    .b(decimal_decoder_2_dout[4]), .e(decimal_decoder_2_dout[23]), .d(decimal_decoder_2_dout[22]),
    .c(decimal_decoder_2_dout[21]), .dp(decimal_decoder_2_dout[20]));
  assign bitselector_1_out = Counter_OE ? Content_Of_Counter : 4'bz;  // Controlled_Buffer controlled_buffer_2
  _7_Segment_Display u_7_segment_display_6 (
    .g(decimal_decoder_1_dout[7]), .f(decimal_decoder_1_dout[6]), .a(decimal_decoder_1_dout[5]),
    .b(decimal_decoder_1_dout[4]), .e(decimal_decoder_1_dout[23]), .d(decimal_decoder_1_dout[22]),
    .c(decimal_decoder_1_dout[21]), .dp(decimal_decoder_1_dout[20]));
  _7_Segment_Display u_7_segment_display_7 (
    .g(decimal_decoder_1_dout[3]), .f(decimal_decoder_1_dout[2]), .a(decimal_decoder_1_dout[1]),
    .b(decimal_decoder_1_dout[0]), .e(decimal_decoder_1_dout[19]), .d(decimal_decoder_1_dout[18]),
    .c(decimal_decoder_1_dout[17]), .dp(decimal_decoder_1_dout[16]));
  _7_Segment_Display u_7_segment_display_8 (
    .g(decimal_decoder_2_dout[3]), .f(decimal_decoder_2_dout[2]), .a(decimal_decoder_2_dout[1]),
    .b(decimal_decoder_2_dout[0]), .e(decimal_decoder_2_dout[19]), .d(decimal_decoder_2_dout[18]),
    .c(decimal_decoder_2_dout[17]), .dp(decimal_decoder_2_dout[16]));
  Decimal_Decoder decimal_decoder_2 (
    .in_1(Reg_B_Content),
    .Dout({decimal_decoder_2_dout[31:28], decimal_decoder_2_dout[31:28], decimal_decoder_2_dout[23:0]}));
  MAR MAR_1 (
    .OE(OE_MAR), .Clock(OE_MBR), .WE(WE_MAR), .Din(bitselector_1_out), .Storade_Data(MAR_Content),
    .Dout(undriven_2));
  Registrador Output_Register (
    .OE(OE_Output), .Clock(OE_MBR), .WE(WE_Output), .Din(controlled_buffer_1_out), .Storade_Data(out_23),
    .Dout(controlled_buffer_1_out));
  assign bit_extender_1_out = {{4{Content_Of_Counter[3]}}, Content_Of_Counter};  // Bit_Extender bit_extender_1
  _7_Segment_Display u_7_segment_display_9 (
    .g(decimal_decoder_3_dout[3]), .f(decimal_decoder_3_dout[2]), .a(decimal_decoder_3_dout[1]),
    .b(decimal_decoder_3_dout[0]), .e(decimal_decoder_3_dout[19]), .d(decimal_decoder_3_dout[18]),
    .c(decimal_decoder_3_dout[17]), .dp(decimal_decoder_3_dout[16]));
  Decimal_Decoder decimal_decoder_3 (.in_1(bit_extender_1_out), .Dout(decimal_decoder_3_dout));
  _7_Segment_Display u_7_segment_display_10 (
    .g(decimal_decoder_4_dout[15]), .f(decimal_decoder_4_dout[14]), .a(decimal_decoder_4_dout[13]),
    .b(decimal_decoder_4_dout[12]), .e(decimal_decoder_4_dout[31]), .d(decimal_decoder_4_dout[30]),
    .c(decimal_decoder_4_dout[29]), .dp(decimal_decoder_4_dout[28]));
  _7_Segment_Display u_7_segment_display_11 (
    .g(decimal_decoder_4_dout[11]), .f(decimal_decoder_4_dout[10]), .a(decimal_decoder_4_dout[9]),
    .b(decimal_decoder_4_dout[8]), .e(decimal_decoder_4_dout[31]), .d(decimal_decoder_4_dout[30]),
    .c(decimal_decoder_4_dout[29]), .dp(decimal_decoder_4_dout[28]));
  _7_Segment_Display u_7_segment_display_12 (
    .g(decimal_decoder_4_dout[7]), .f(decimal_decoder_4_dout[6]), .a(decimal_decoder_4_dout[5]),
    .b(decimal_decoder_4_dout[4]), .e(decimal_decoder_4_dout[23]), .d(decimal_decoder_4_dout[22]),
    .c(decimal_decoder_4_dout[21]), .dp(decimal_decoder_4_dout[20]));
  _7_Segment_Display u_7_segment_display_13 (
    .g(decimal_decoder_4_dout[3]), .f(decimal_decoder_4_dout[2]), .a(decimal_decoder_4_dout[1]),
    .b(decimal_decoder_4_dout[0]), .e(decimal_decoder_4_dout[19]), .d(decimal_decoder_4_dout[18]),
    .c(decimal_decoder_4_dout[17]), .dp(decimal_decoder_4_dout[16]));
  Decimal_Decoder decimal_decoder_4 (
    .in_1(out_23),
    .Dout({decimal_decoder_4_dout[31:28], decimal_decoder_4_dout[31:28], decimal_decoder_4_dout[23:0]}));
  RAM #(.addrWidth(4)) ram_1 (
    .addr(undriven_2), .we(WE_RAM), .oe(OE_RAM), .clk(OE_MBR), .din(controlled_buffer_1_out),
    .dout(controlled_buffer_1_out));

  // Notes on the sheet:
  //   External Data Bus
  //   Internal Data Bus
  //   Internal Address Bus (4 bits)
  //   External Address Bus
endmodule

module Memory_Cell (
  input  Clock,
  input  WE,
  input  Dout,
  input  Stored_data,
  input  Din,
  input  OE,
  input  Reset
);

  wire and_1_out, and_2_out, not_1_out, or_1_out;

  not not_1 (not_1_out, WE);
  and and_1 (and_1_out, Stored_data, not_1_out);
  and and_2 (and_2_out, WE, Din);
  or or_1 (or_1_out, and_1_out, and_2_out);
  D_Flip_Flop d_ff_1 (.D(or_1_out), .clk(Clock), .Q(Stored_data), .reset(Reset));  // open: Qn, preset
  assign Dout = OE ? Stored_data : 1'bz;  // Controlled_Buffer controlled_buffer_1

  // Notes on the sheet:
  //   Memory Cell
endmodule

module Registrador (
  input  OE,
  input  Clock,
  input  WE,
  input  [7:0] Din,
  input  [7:0] Storade_Data,
  input  [7:0] Dout
);

  wire One_p7;

  Memory_Cell Zero (
    .Clock(Clock), .WE(WE), .Dout(Dout[0]), .Stored_data(Storade_Data[0]), .Din(Din[0]), .OE(OE));  // open: Reset
  // Memory_Cell One: pin names not known; wires that end beside it: Clock, WE, Dout[1], Storade_Data[1], Din[1], OE, One_p7, One_p7
  Memory_Cell Two (
    .Clock(Clock), .WE(WE), .Dout(Dout[2]), .Stored_data(Storade_Data[2]), .Din(Din[2]), .OE(OE));  // open: Reset
  Memory_Cell Three (
    .Clock(Clock), .WE(WE), .Dout(Dout[3]), .Stored_data(Storade_Data[3]), .Din(Din[3]), .OE(OE));  // open: Reset
  Memory_Cell Four (
    .Clock(Clock), .WE(WE), .Dout(Dout[4]), .Stored_data(Storade_Data[4]), .Din(Din[4]), .OE(OE));  // open: Reset
  Memory_Cell Five (
    .Clock(Clock), .WE(WE), .Dout(Dout[5]), .Stored_data(Storade_Data[5]), .Din(Din[5]), .OE(OE));  // open: Reset
  Memory_Cell Six (
    .Clock(Clock), .WE(WE), .Dout(Dout[6]), .Stored_data(Storade_Data[6]), .Din(Din[6]), .OE(OE));  // open: Reset
  Memory_Cell Seven (
    .Clock(Clock), .WE(WE), .Dout(Dout[7]), .Stored_data(Storade_Data[7]), .Din(Din[7]), .OE(OE));  // open: Reset

  // Notes on the sheet:
  //   Register (8bits)
endmodule

module MAR (
  input  OE,
  input  Clock,
  input  WE,
  input  [3:0] Din,
  input  [3:0] Storade_Data,
  input  [3:0] Dout
);

  wire One_p7;

  Memory_Cell Zero (
    .Clock(Clock), .WE(WE), .Dout(Dout[0]), .Stored_data(Storade_Data[0]), .Din(Din[0]), .OE(OE));  // open: Reset
  // Memory_Cell One: pin names not known; wires that end beside it: Clock, WE, Dout[1], Storade_Data[1], Din[1], OE, One_p7, One_p7
  Memory_Cell Two (
    .Clock(Clock), .WE(WE), .Dout(Dout[2]), .Stored_data(Storade_Data[2]), .Din(Din[2]), .OE(OE));  // open: Reset
  Memory_Cell Three (
    .Clock(Clock), .WE(WE), .Dout(Dout[3]), .Stored_data(Storade_Data[3]), .Din(Din[3]), .OE(OE));  // open: Reset

  // Notes on the sheet:
  //   MAR
endmodule

module ALU (
  input  [7:0] Reg_A,
  input  [7:0] Dout,
  input  [7:0] Reg_B,
  input  OE,
  input  Carry_Out,
  output [7:0] ALU_Result
);

  Adder adder_1 (.a(Reg_A), .b(Reg_B), .out(ALU_Result), .cout(Carry_Out));  // open: cin
  assign Dout = OE ? ALU_Result : 8'bz;  // Controlled_Buffer controlled_buffer_1

  // Notes on the sheet:
  //   ALU (8 bits)
endmodule

module Decimal_Decoder (
  input  [7:0] in_1,
  output [31:0] Dout
);

  ROM #(.dataWidth(32)) rom_1 (
    .addr(in_1),
    .data({Dout[31:28], Dout[15:12], Dout[27:24], Dout[11:8], Dout[23:20], Dout[7:4], Dout[19:16], Dout[3:0]}));

  // Notes on the sheet:
  //   Decimal_Decoder
  //   contents of rom_1 (hex, n*v repeats v):
  //   e7 21 cb 6b 2d 6e ee 23 ef 2f 21e7 2121 21cb 216b 212d 216e 21ee 2123 21ef 212f cbe7 cb21 cbcb cb6b
  //   cb2d cb6e cbee cb23 cbef cb2f 6be7 6b21 6bcb 6b6b 6b2d 6b6e 6bee 6b23 6bef 6b2f 2de7 2d21 2dcb 2d6b
  //   2d2d 2d6e 2dee 2d23 2def 2d2f 6ee7 6e21 6ecb 6e6b 6e2d 6e6e 6eee 6e23 6eef 6e2f eee7 ee21 eecb ee6b
  //   ee2d ee6e eeee ee23 eeef ee2f 23e7 2321 23cb 236b 232d 236e 23ee 2323 23ef 232f efe7 ef21 efcb ef6b
  //   ef2d ef6e efee ef23 efef ef2f 2fe7 2f21 2fcb 2f6b 2f2d 2f6e 2fee 2f23 2fef 2f2f 21e7e7 21e721 21e7cb
  //   21e76b 21e72d 21e76e 21e7ee 21e723 21e7ef 21e72f 2121e7 212121 2121cb 21216b 21212d 21216e 2121ee
  //   212123 2121ef 21212f 21cbe7 21cb21 21cbcb 21cb6b 21cb2d 21cb6e 21cbee 21cb23 21cbef 21cb2f 216be7
  //   216b21 216bcb 216b6b 216b2d 216b6e 216bee 216b23 216bef 216b2f 212de7 212d21 212dcb 212d6b 212d2d
  //   212d6e 212dee 212d23 212def 212d2f 216ee7 216e21 216ecb 216e6b 216e2d 216e6e 216eee 216e23 216eef
  //   216e2f 21eee7 21ee21 21eecb 21ee6b 21ee2d 21ee6e 21eeee 21ee23 21eeef 21ee2f 2123e7 212321 2123cb
  //   21236b 21232d 21236e 2123ee 212323 2123ef 21232f 21efe7 21ef21 21efcb 21ef6b 21ef2d 21ef6e 21efee
  //   21ef23 21efef 21ef2f 212fe7 212f21 212fcb 212f6b 212f2d 212f6e 212fee 212f23 212fef 212f2f cbe7e7
  //   cbe721 cbe7cb cbe76b cbe72d cbe76e cbe7ee cbe723 cbe7ef cbe72f cb21e7 cb2121 cb21cb cb216b cb212d
  //   cb216e cb21ee cb2123 cb21ef cb212f cbcbe7 cbcb21 cbcbcb cbcb6b cbcb2d cbcb6e cbcbee cbcb23 cbcbef
  //   cbcb2f cb6be7 cb6b21 cb6bcb cb6b6b cb6b2d cb6b6e cb6bee cb6b23 cb6bef cb6b2f cb2de7 cb2d21 cb2dcb
  //   cb2d6b cb2d2d cb2d6e cb2dee cb2d23 cb2def cb2d2f cb6ee7 cb6e21 cb6ecb cb6e6b cb6e2d cb6e6e
endmodule
